# Fritzing sketch Buzzer_sensor (saved by Fritzing 0.9.3b)

parts:
  WeMos_D1_R1 = WeMos D1 R2
  J1 = Camdenboss CTB0158-3 [part_number=CTB0158-3 package=THT]

nets:
  N1: WeMos_D1_R1.D12, J1.terminal_2
  N2: WeMos_D1_R1.GND, J1.terminal_3
  N3: WeMos_D1_R1.5V, J1.terminal_1

notes:
  VCC
  GND
  I/O
  Buzzer Sensor

custom parts:
  WeMos D1 R2: The D1 R2 is a mini wifi board based on the ESP-8266EX.
