# Fritzing sketch GasSensor (saved by Fritzing 0.9.3b)

parts:
  WeMos_D1_R1 = WeMos D1 R2
  부품1 = MQ-3 breakout

nets:
  N1: WeMos_D1_R1.A0, 부품1.AO
  GND: WeMos_D1_R1.GND, 부품1.GND
  5V: WeMos_D1_R1.5V, 부품1.VCC

custom parts:
  WeMos D1 R2: The D1 R2 is a mini wifi board based on the ESP-8266EX.
  MQ-3 breakout: Alcohol sensor is capable of detecting alcohol (ethanol) particles on itself and gives the information in digital form back to us to manipulate with it. SKU:101251 • Voltage: 5V DC • Power: max 750mW • Measurement range: 0.04-4mg/L
