# Fritzing sketch 4LED_DHT11_bb (saved by Fritzing 0.9.3b)
breadboards: 1

parts:
  WeMos_D1_R1 = WeMos D1 R2
  Grove1 = Grove 4 Digit Display
  DHT1 = DHT11 Humitidy and Temperature Sensor

nets:
  N1: WeMos_D1_R1.D2, DHT1.DATA
  N2: WeMos_D1_R1.D3, Grove1.CLK
  N3: WeMos_D1_R1.D4, Grove1.DIO
  GND: WeMos_D1_R1.GND, Grove1.GND, DHT1.GND
  5V: WeMos_D1_R1.5V, Grove1.VCC, DHT1.VDD

custom parts:
  WeMos D1 R2: The D1 R2 is a mini wifi board based on the ESP-8266EX.
  DHT11 Humitidy and Temperature Sensor: DHT11 Humidity and Temperature Sensor
