# Fritzing sketch Barometric_sensor (saved by Fritzing 0.9.3b)

parts:
  WeMos_D1_R1 = WeMos D1 R2
  부품1 = Barometric Pressure Sensor - BMP180 Breakout (GY-68)

nets:
  N1: WeMos_D1_R1.D14, 부품1.VCC
  N2: WeMos_D1_R1.D15, 부품1.GND
  N3: WeMos_D1_R1.GND, 부품1.SCL
  N4: WeMos_D1_R1.5V, 부품1.SDA

notes:
  SCL
  GND
  SDA
  VCC
  기압센서

custom parts:
  WeMos D1 R2: The D1 R2 is a mini wifi board based on the ESP-8266EX.
