# Fritzing sketch Caynene_DHT11_LED (saved by Fritzing 0.9.3b)
breadboards: 1

parts:
  WeMos_D1_R1 = WeMos D1 R2
  DHT1 = DHT11 Humitidy and Temperature Sensor
  LED1 = LED - 5mm [color="Red (633nm)" package="5 mm [THT]"]
  R1 = Resistor [tolerance=±5% resistance=220 package=THT]

nets:
  N1: WeMos_D1_R1.D2, DHT1.NULL
  N2: WeMos_D1_R1.D3, LED1.anode
  GND: WeMos_D1_R1.GND, DHT1.GND, R1.Pin_0
  5V: WeMos_D1_R1.5V, DHT1.VDD
  N3: LED1.cathode, R1.Pin_1

notes:
  VCC
  GND
  DATA

custom parts:
  WeMos D1 R2: The D1 R2 is a mini wifi board based on the ESP-8266EX.
  DHT11 Humitidy and Temperature Sensor: DHT11 Humidity and Temperature Sensor
