# Fritzing sketch 4LED_bb (saved by Fritzing 0.9.3b)
breadboards: 1

parts:
  WeMos_D1_R1 = WeMos D1 R2
  LED1 = LED - 5mm [color="Red (633nm)" package="5 mm [THT]"]
  R2 = Resistor [tolerance=±5% resistance=200 package=THT]
  LED2 = LED - 5mm [color="Orange (620nm)" package="5 mm [THT]"]
  LED3 = LED - 5mm [color="Green (565nm)" package="5 mm [THT]"]
  LED4 = LED - 5mm [color="Blue (470nm)" package="5 mm [THT]"]
  R3 = Resistor [tolerance=±5% resistance=200 package=THT]
  R4 = Resistor [tolerance=±5% resistance=200 package=THT]
  R5 = Resistor [tolerance=±5% resistance=200 package=THT]

nets:
  N1: WeMos_D1_R1.D2, LED4.anode
  N2: WeMos_D1_R1.D3, LED3.anode
  N3: WeMos_D1_R1.D4, LED2.anode
  N4: WeMos_D1_R1.(D5), LED1.anode
  N5: WeMos_D1_R1.GND, R2.Pin_1, R3.Pin_1, R4.Pin_1, R5.Pin_1
  N6: LED1.cathode, R2.Pin_0
  N7: LED2.cathode, R3.Pin_0
  N8: LED3.cathode, R4.Pin_0
  N9: LED4.cathode, R5.Pin_0

custom parts:
  WeMos D1 R2: The D1 R2 is a mini wifi board based on the ESP-8266EX.
