# Fritzing sketch Sound_detector (saved by Fritzing 0.9.3b)
breadboards: 1

parts:
  WeMos_D1_R1 = WeMos D1 R2
  J1 = Camdenboss CTB0158-3 [part_number=CTB0158-3 package=THT]
  LED1 = LED - 5mm [color="Red (633nm)" package="5 mm [THT]"]
  R1 = Resistor [tolerance=±5% resistance=220 package=THT]

nets:
  N1: WeMos_D1_R1.D2, J1.terminal_1
  N2: WeMos_D1_R1.GND, J1.terminal_2, LED1.cathode
  N3: WeMos_D1_R1.5V, J1.terminal_3
  N4: LED1.anode, R1.Pin_1

notes:
  VCC
  GND
  OUT
  Sound Sensor

custom parts:
  WeMos D1 R2: The D1 R2 is a mini wifi board based on the ESP-8266EX.
