# Fritzing sketch PIR센서 (saved by Fritzing 0.9.3b)

parts:
  WeMos_D1_R1 = WeMos D1 R2
  Sensore_PIR_HC-SR502 = HC-SR501 Body Sensor Module

nets:
  N1: WeMos_D1_R1.D2, Sensore_PIR_HC-SR502.OUT
  GND: WeMos_D1_R1.GND, Sensore_PIR_HC-SR502.GND
  5V: WeMos_D1_R1.5V, Sensore_PIR_HC-SR502.VCC

custom parts:
  WeMos D1 R2: The D1 R2 is a mini wifi board based on the ESP-8266EX.
  HC-SR501 Body Sensor Module: Pyroelectric Infrared PIR Motion Sensor Detector Module
