# Fritzing sketch lcd(16x2)_Temperature_sensor (saved by Fritzing 0.9.3b)
breadboards: 1

parts:
  WeMos_D1_R1 = WeMos D1 R2
  LCM1602_IIC2 = LCM1602 IIC [part_number="LCM1602 IIC" chip_label="LCM1602 IIC" package="DIP (Dual Inline) [THT]"]
  LCD2 = LCD screen
  DHT1 = DHT11 Humitidy and Temperature Sensor

nets:
  N1: WeMos_D1_R1.D3, LCM1602_IIC2.SCL
  N2: WeMos_D1_R1.D4, LCM1602_IIC2.SDA
  N3: WeMos_D1_R1.(D7), DHT1.NULL
  GND: WeMos_D1_R1.GND, LCM1602_IIC2.GND, DHT1.GND
  5V: WeMos_D1_R1.5V, LCM1602_IIC2.VCC, DHT1.VDD
  VSS: LCM1602_IIC2.VSS, LCD2.VSS
  VDD: LCM1602_IIC2.VDD, LCD2.VDD
  N4: LCM1602_IIC2.V0, LCD2.V0
  N5: LCM1602_IIC2.RS, LCD2.RS
  N6: LCM1602_IIC2.RW, LCD2.R/W
  N7: LCM1602_IIC2.E, LCD2.E
  N8: LCM1602_IIC2.D0, LCD2.DB0
  N9: LCM1602_IIC2.D1, LCD2.DB1
  N10: LCM1602_IIC2.D2, LCD2.DB2
  N11: LCM1602_IIC2.D3, LCD2.DB3
  N12: LCM1602_IIC2.D4, LCD2.DB4
  N13: LCM1602_IIC2.D5, LCD2.DB5
  N14: LCM1602_IIC2.D6, LCD2.DB6
  N15: LCM1602_IIC2.D7, LCD2.DB7
  N16: LCM1602_IIC2.A, LCD2.LED+
  N17: LCM1602_IIC2.K, LCD2.LED-

custom parts:
  WeMos D1 R2: The D1 R2 is a mini wifi board based on the ESP-8266EX.
  LCM1602 IIC: I2C-Module to use a 1602 or 2004 LCD on with the wire.h libory Serial LCD Modul
  DHT11 Humitidy and Temperature Sensor: DHT11 Humidity and Temperature Sensor
