# Fritzing sketch potentiometer_bb (saved by Fritzing 0.9.3b)
breadboards: 1

parts:
  WeMos_D1_R1 = WeMos D1 R2
  R1 = Rotary Potentiometer (Small) [maximum_resistance=100kΩ package=THT]
  LED1 = LED - 5mm [color="Red (633nm)" package="5 mm [THT]"]
  R2 = Resistor [tolerance=±5% resistance=200 package=THT]

nets:
  N1: WeMos_D1_R1.D2, LED1.anode
  N2: WeMos_D1_R1.GND#15, R2.Pin_0
  N3: WeMos_D1_R1.A0, R1.wiper
  N4: WeMos_D1_R1.GND#21, R1.leg1
  N5: WeMos_D1_R1.5V, R1.leg2
  N6: LED1.cathode, R2.Pin_1

notes:
  potentiometer

custom parts:
  WeMos D1 R2: The D1 R2 is a mini wifi board based on the ESP-8266EX.
