# Fritzing sketch relay_module_bb (saved by Fritzing 0.9.3b)
breadboards: 1

parts:
  WeMos_D1_R1 = WeMos D1 R2
  R2 = Resistor [tolerance=±5% resistance=200 package=THT]
  WeMos_D1_Mini_Relay_Shield_V1 = WeMos D1 Mini Relay Shield V2  # not connected
  S1 = SWITCH-MOMENTARY-2 [package=tactile-pth]

nets:
  N1: WeMos_D1_R1.D3, S1.2
  N2: WeMos_D1_R1.GND, R2.Pin_1
  N3: WeMos_D1_R1.5V, S1.1

custom parts:
  WeMos D1 R2: The D1 R2 is a mini wifi board based on the ESP-8266EX.
