# Fritzing sketch Soil_moisture_sensor (saved by Fritzing 0.9.3b)

parts:
  WeMos_D1_R1 = WeMos D1 R2
  부품1 = Soil Moisture Sensor
  J1 = Camdenboss CTB0158-4 [part_number=CTB0158-4 package=THT]
  J3 = Screw terminal - 2 pins [package=THT]

nets:
  N1: WeMos_D1_R1.A0, J1.terminal_4
  N2: WeMos_D1_R1.GND, J1.terminal_2
  N3: WeMos_D1_R1.5V, J1.terminal_1
  N4: 부품1.GND, J3.pin2
  N5: 부품1.VCC, J3.pin1

custom parts:
  WeMos D1 R2: The D1 R2 is a mini wifi board based on the ESP-8266EX.
