# Fritzing sketch Temp_Humi_DHT11 (saved by Fritzing 0.9.3b)

parts:
  WeMos_D1_R1 = WeMos D1 R2
  DHT1 = DHT11 Humitidy and Temperature Sensor

nets:
  N1: WeMos_D1_R1.D2, DHT1.NULL
  GND: WeMos_D1_R1.GND, DHT1.GND
  5V: WeMos_D1_R1.5V, DHT1.VDD

notes:
  VCC
  GND
  DATA

custom parts:
  WeMos D1 R2: The D1 R2 is a mini wifi board based on the ESP-8266EX.
  DHT11 Humitidy and Temperature Sensor: DHT11 Humidity and Temperature Sensor
