# Fritzing sketch PM_sensor_fzz (saved by Fritzing 0.9.3b)

parts:
  WeMos_D1_R1 = WeMos D1 R2
  J1 = Camdenboss CTB0158-8 [part_number=CTB0158-8 package=THT]

nets:
  N1: WeMos_D1_R1.D0/RX, J1.terminal_3
  N2: WeMos_D1_R1.D1/TX, J1.terminal_4
  N3: WeMos_D1_R1.GND, J1.terminal_8
  N4: WeMos_D1_R1.5V, J1.terminal_7

notes:
  VCC
  GND
  RX
  PM_Sensor
  TX

custom parts:
  WeMos D1 R2: The D1 R2 is a mini wifi board based on the ESP-8266EX.
