# Fritzing sketch Tilt_sensor_bb (saved by Fritzing 0.9.3b)
breadboards: 1

parts:
  WeMos_D1_R1 = WeMos D1 R2
  LED1 = LED - 5mm [color="Red (633nm)" package="5 mm [THT]"]
  R1 = Resistor [tolerance=±5% resistance=220 package=THT]
  J1 = JST-B3P-VH [part_number=JST-B3P-VH package=THT]

nets:
  N1: WeMos_D1_R1.D2, J1.pin1
  N2: WeMos_D1_R1.D3, LED1.anode
  N3: WeMos_D1_R1.GND, R1.Pin_0, J1.pin2
  N4: WeMos_D1_R1.5V, J1.pin3
  N5: LED1.cathode, R1.Pin_1

notes:
  Tilt sensor

custom parts:
  WeMos D1 R2: The D1 R2 is a mini wifi board based on the ESP-8266EX.
