# Fritzing sketch UV_sensor_bb (saved by Fritzing 0.9.3b)

parts:
  WeMos_D1_R1 = WeMos D1 R2
  J1 = Camdenboss CTB0158-5 [part_number=CTB0158-5 package=THT]

nets:
  N1: WeMos_D1_R1.A0, J1.pin2
  N2: WeMos_D1_R1.GND, J1.pin3
  N3: WeMos_D1_R1.3.3V, J1.pin4

notes:
  3.3V
  GND
  OUT

custom parts:
  WeMos D1 R2: The D1 R2 is a mini wifi board based on the ESP-8266EX.
